# Fritzing sketch Water_Sensor_Schematic_v1 (saved by Fritzing 0.7.12b)
breadboards: 1

parts:
  RaspberryPi1 = Raspberry Pi Model B
  J1 = Piezo Speaker
  C1 = Electrolytic Capacitor [capacitance=10µF voltage=20V package="100 mil [THT, electrolytic]"]
  S1 = Pushbutton [package=THT]

nets:
  N1: RaspberryPi1.3V3, S1.leg1
  N2: RaspberryPi1.GND, RaspberryPi1.TXD, RaspberryPi1.#18, J1.pin1, C1.-, C1.+, S1.leg0
  N3: RaspberryPi1.#17, RaspberryPi1.#21, J1.pin2

custom parts:
  Raspberry Pi Model B: Raspberry Pi (Model B)
